// Logisim project fibonacci.circ as structural Verilog: 2 circuits, main circuit main
module main (
  input  [2:0] in_1,
  output [3:0] out_2
);

  wire clock_1_out, comparator_1_eq;
  wire [2:0] counter_1_q;
  wire [3:0] f_add_1_fn;

  Clock clock_1 (.out(clock_1_out));
  Counter #(.width(3), .max('h7), .ongoal("stay")) counter_1 (
    .Q(counter_1_q), .clk(clock_1_out));  // open: load, D, count, carry, clr
  // Probe on counter_1_q
  Comparator #(.width(3)) comparator_1 (.a(in_1), .b(counter_1_q), .eq(comparator_1_eq));  // open: gt, lt
  F_add f_add_1 (.clock(clock_1_out), .Fn(f_add_1_fn));
  // Probe on f_add_1_fn
  Register #(.width(4)) register_1 (.D(f_add_1_fn), .Q(out_2), .clk(comparator_1_eq));  // open: en, clr
endmodule

module F_add (
  input  clock,
  output [3:0] Fn
);

  wire counter_1_carry, not_1_out;
  wire [3:0] adder_1_out, multiplexer_1_out, register_1_q;

  Counter #(.width(1), .max('h1), .ongoal("stay")) counter_1 (
    .carry(counter_1_carry), .clk(clock));  // open: load, D, count, Q, clr
  not not_1 (not_1_out, counter_1_carry);
  Multiplexer #(.width(4)) multiplexer_1 (
    .in0(register_1_q), .in1(4'b0001), .out(multiplexer_1_out), .sel(not_1_out));  // open: en
  // Probe on multiplexer_1_out
  // Probe on Fn
  Adder #(.width(4)) adder_1 (.a(multiplexer_1_out), .b(Fn), .out(adder_1_out));  // open: cin, cout
  Register #(.width(4)) register_1 (.D(adder_1_out), .Q(register_1_q), .clk(clock));  // open: en, clr
  Register #(.width(4)) register_2 (.D(multiplexer_1_out), .Q(Fn), .clk(clock));  // open: en, clr
endmodule
