// Logisim project fibonacci_up.circ as structural Verilog: 7 circuits, main circuit main
module main (
  input  [31:0] in_1,
  output [31:0] out_2
);

  wire clock_1_out, counter_1_q, counter_2_q, multiplexer_1_out, multiplexer_6_out, onebit_1_out_3,
       onebit_1_out_4;
  wire [31:0] E0, E1, E2, E3, judge_1_out_6, judge_1_out_7, judge_1_out_8, judge_1_out_9, matrix_1_out_2,
       matrix_1_out_3, matrix_1_out_4, matrix_1_out_5, matrix_mult_1_out_9, matrix_mult_1_out_10,
       matrix_mult_1_out_11, matrix_mult_1_out_12, multiplexer_2_out, multiplexer_3_out, multiplexer_4_out,
       multiplexer_5_out, unit_matr_1_out_1, unit_matr_1_out_2, unit_matr_1_out_3, unit_matr_1_out_4;

  Clock clock_1 (.out(clock_1_out));
  unit_matr unit_matr_1 (
    .out_1(unit_matr_1_out_1), .out_2(unit_matr_1_out_2), .out_3(unit_matr_1_out_3), .out_4(unit_matr_1_out_4));
  onebit onebit_1 (.in_1(in_1), .in_2(clock_1_out), .out_3(onebit_1_out_3), .out_4(onebit_1_out_4));
  Counter #(.width(1), .max('h1), .ongoal("stay"), .trigger("falling")) counter_1 (
    .Q(counter_1_q), .clk(clock_1_out));  // open: load, D, count, carry, clr
  Multiplexer multiplexer_1 (
    .in0(clock_1_out), .in1(counter_2_q), .out(multiplexer_1_out), .sel(counter_2_q));  // open: en
  Counter #(.width(1), .max('h1), .ongoal("stay")) counter_2 (
    .Q(counter_2_q), .clk(onebit_1_out_4));  // open: load, D, count, carry, clr
  Multiplexer #(.width(32)) multiplexer_2 (
    .in0(unit_matr_1_out_1), .in1(E0), .out(multiplexer_2_out), .sel(counter_1_q));  // open: en
  Multiplexer #(.width(32)) multiplexer_3 (
    .in0(unit_matr_1_out_2), .in1(E1), .out(multiplexer_3_out), .sel(counter_1_q));  // open: en
  Multiplexer #(.width(32)) multiplexer_4 (
    .in0(unit_matr_1_out_3), .in1(E2), .out(multiplexer_4_out), .sel(counter_1_q));  // open: en
  Multiplexer #(.width(32)) multiplexer_5 (
    .in0(unit_matr_1_out_4), .in1(E3), .out(multiplexer_5_out), .sel(counter_1_q));  // open: en
  Multiplexer multiplexer_6 (
    .in0(onebit_1_out_3), .in1(onebit_1_out_4), .out(multiplexer_6_out), .sel(counter_2_q));  // open: en
  matrix matrix_1 (
    .in_1(multiplexer_1_out), .out_2(matrix_1_out_2), .out_3(matrix_1_out_3), .out_4(matrix_1_out_4),
    .out_5(matrix_1_out_5));
  judge judge_1 (
    .in_1(multiplexer_6_out), .in_2(matrix_1_out_2), .in_3(matrix_1_out_3), .in_4(matrix_1_out_4),
    .in_5(matrix_1_out_5), .out_6(judge_1_out_6), .out_7(judge_1_out_7), .out_8(judge_1_out_8),
    .out_9(judge_1_out_9));
  matrix_mult matrix_mult_1 (
    .A0(judge_1_out_6), .A1(judge_1_out_7), .A2(judge_1_out_8), .A3(judge_1_out_9), .B0(multiplexer_2_out),
    .B1(multiplexer_3_out), .B2(multiplexer_4_out), .B3(multiplexer_5_out), .out_9(matrix_mult_1_out_9),
    .out_10(matrix_mult_1_out_10), .out_11(matrix_mult_1_out_11), .out_12(matrix_mult_1_out_12));
  Register #(.width(32)) register_1 (.D(matrix_mult_1_out_9), .Q(E0), .clk(multiplexer_1_out));  // open: en, clr
  Register #(.width(32)) register_2 (.D(matrix_mult_1_out_10), .Q(E1), .clk(multiplexer_1_out));  // open: en, clr
  Register #(.width(32)) register_3 (.D(matrix_mult_1_out_11), .Q(E2), .clk(multiplexer_1_out));  // open: en, clr
  Register #(.width(32)) register_4 (.D(matrix_mult_1_out_12), .Q(E3), .clk(multiplexer_1_out));  // open: en, clr
  Multiplexer #(.width(32)) multiplexer_7 (
    .in0({32{1'b0}}), .in1(matrix_mult_1_out_9), .sel(onebit_1_out_4));  // open: out, en
  Multiplexer #(.width(32)) multiplexer_8 (
    .in0({32{1'b0}}), .in1(matrix_mult_1_out_10), .out(out_2), .sel(onebit_1_out_4));  // open: en
  Multiplexer #(.width(32)) multiplexer_9 (
    .in0({32{1'b0}}), .in1(matrix_mult_1_out_11), .sel(onebit_1_out_4));  // open: out, en
  Multiplexer #(.width(32)) multiplexer_10 (
    .in0({32{1'b0}}), .in1(matrix_mult_1_out_12), .sel(onebit_1_out_4));  // open: out, en
endmodule

module onebit (
  input  [31:0] in_1,
  input  in_2,
  output out_3,
  output out_4
);

  wire counter_1_q;
  wire [0:0] multiplexer_1_out_2;
  wire [30:0] multiplexer_1_out;
  wire [31:0] register_2_q;

  Counter #(.width(1), .max('h1), .ongoal("stay")) counter_1 (
    .Q(counter_1_q), .clk(in_2));  // open: load, D, count, carry, clr
  Multiplexer #(.width(32)) multiplexer_1 (
    .in0(in_1), .in1(register_2_q), .out({multiplexer_1_out, multiplexer_1_out_2[0]}), .sel(counter_1_q));  // open: en
  Register #(.width(1)) register_1 (.D(multiplexer_1_out_2[0]), .Q(out_3), .clk(in_2));  // open: en, clr
  Comparator #(.width(32)) comparator_1 (
    .a({32{1'b0}}), .b({multiplexer_1_out, multiplexer_1_out_2[0]}), .eq(out_4));  // open: gt, lt
  Register #(.width(32)) register_2 (.D({1'b0, multiplexer_1_out}), .Q(register_2_q), .clk(in_2));  // open: en, clr
endmodule

module count_comp (
  input  [31:0] in_1,
  input  in_2,
  output out_3,
  output out_4
);

  wire counter_2_carry;
  wire [31:0] counter_1_q;

  Counter #(.width(32), .max('hffffffff), .ongoal("stay")) counter_1 (
    .Q(counter_1_q), .clk(in_2));  // open: load, D, count, carry, clr
  Comparator #(.width(32)) comparator_1 (.a(in_1), .b(counter_1_q), .eq(out_4));  // open: gt, lt
  Counter #(.width(1), .max('h1), .ongoal("stay")) counter_2 (
    .carry(counter_2_carry), .clk(out_4));  // open: load, D, count, Q, clr
  Multiplexer multiplexer_1 (.in0(in_2), .in1(counter_2_carry), .out(out_3), .sel(counter_2_carry));  // open: en
endmodule

module matrix_mult (
  input  [31:0] A0,
  input  [31:0] A1,
  input  [31:0] A2,
  input  [31:0] A3,
  input  [31:0] B0,
  input  [31:0] B1,
  input  [31:0] B2,
  input  [31:0] B3,
  output [31:0] out_9,
  output [31:0] out_10,
  output [31:0] out_11,
  output [31:0] out_12
);

  wire [31:0] multiplier_1_out, multiplier_2_out, multiplier_3_out, multiplier_4_out, multiplier_5_out,
       multiplier_6_out, multiplier_7_out, multiplier_8_out;

  Multiplier #(.width(32)) multiplier_1 (.a(A0), .b(B0), .out(multiplier_1_out));  // open: cin, cout
  Multiplier #(.width(32)) multiplier_2 (.a(A1), .b(B2), .out(multiplier_2_out));  // open: cin, cout
  Multiplier #(.width(32)) multiplier_3 (.a(A2), .b(B1), .out(multiplier_3_out));  // open: cin, cout
  Multiplier #(.width(32)) multiplier_4 (.a(A3), .b(B3), .out(multiplier_4_out));  // open: cin, cout
  Multiplier #(.width(32)) multiplier_5 (.a(B0), .b(A2), .out(multiplier_5_out));  // open: cin, cout
  Multiplier #(.width(32)) multiplier_6 (.a(B1), .b(A0), .out(multiplier_6_out));  // open: cin, cout
  Multiplier #(.width(32)) multiplier_7 (.a(B2), .b(A3), .out(multiplier_7_out));  // open: cin, cout
  Multiplier #(.width(32)) multiplier_8 (.a(B3), .b(A1), .out(multiplier_8_out));  // open: cin, cout
  Adder #(.width(32)) adder_1 (.a(multiplier_1_out), .b(multiplier_2_out), .out(out_9));  // open: cin, cout
  Adder #(.width(32)) adder_2 (.a(multiplier_6_out), .b(multiplier_8_out), .out(out_10));  // open: cin, cout
  Adder #(.width(32)) adder_3 (.a(multiplier_5_out), .b(multiplier_7_out), .out(out_11));  // open: cin, cout
  Adder #(.width(32)) adder_4 (.a(multiplier_3_out), .b(multiplier_4_out), .out(out_12));  // open: cin, cout
endmodule

module unit_matr (
  output [31:0] out_1,
  output [31:0] out_2,
  output [31:0] out_3,
  output [31:0] out_4
);


  assign out_1 = 32'h1;
  assign out_2 = {32{1'b0}};
  assign out_3 = {32{1'b0}};
  assign out_4 = 32'h1;
endmodule

module matrix (
  input  in_1,
  output [31:0] out_2,
  output [31:0] out_3,
  output [31:0] out_4,
  output [31:0] out_5
);

  wire counter_1_q;
  wire [31:0] matrix_mult_1_out_9, matrix_mult_1_out_10, matrix_mult_1_out_11, matrix_mult_1_out_12,
       multiplexer_1_out, multiplexer_2_out, multiplexer_3_out, multiplexer_4_out, multiplexer_5_out,
       multiplexer_6_out, multiplexer_7_out, multiplexer_8_out, unit_matr_1_out_1, unit_matr_1_out_2,
       unit_matr_1_out_3, unit_matr_1_out_4;

  Counter #(.width(1), .max('h1), .ongoal("stay")) counter_1 (
    .Q(counter_1_q), .clk(in_1));  // open: load, D, count, carry, clr
  Multiplexer #(.width(32)) multiplexer_1 (
    .in0(32'h1), .in1(out_2), .out(multiplexer_1_out), .sel(counter_1_q));  // open: en
  Multiplexer #(.width(32)) multiplexer_2 (
    .in0(32'h1), .in1(out_3), .out(multiplexer_2_out), .sel(counter_1_q));  // open: en
  Multiplexer #(.width(32)) multiplexer_3 (
    .in0(32'h1), .in1(out_4), .out(multiplexer_3_out), .sel(counter_1_q));  // open: en
  Multiplexer #(.width(32)) multiplexer_4 (
    .in0({32{1'b0}}), .in1(out_5), .out(multiplexer_4_out), .sel(counter_1_q));  // open: en
  unit_matr unit_matr_1 (
    .out_1(unit_matr_1_out_1), .out_2(unit_matr_1_out_2), .out_3(unit_matr_1_out_3), .out_4(unit_matr_1_out_4));
  Multiplexer #(.width(32)) multiplexer_5 (
    .in0(unit_matr_1_out_1), .in1(out_2), .out(multiplexer_5_out), .sel(counter_1_q));  // open: en
  Multiplexer #(.width(32)) multiplexer_6 (
    .in0(unit_matr_1_out_2), .in1(out_3), .out(multiplexer_6_out), .sel(counter_1_q));  // open: en
  Multiplexer #(.width(32)) multiplexer_7 (
    .in0(unit_matr_1_out_3), .in1(out_4), .out(multiplexer_7_out), .sel(counter_1_q));  // open: en
  Multiplexer #(.width(32)) multiplexer_8 (
    .in0(unit_matr_1_out_4), .in1(out_5), .out(multiplexer_8_out), .sel(counter_1_q));  // open: en
  matrix_mult matrix_mult_1 (
    .A0(multiplexer_1_out), .A1(multiplexer_2_out), .A2(multiplexer_3_out), .A3(multiplexer_4_out),
    .B0(multiplexer_5_out), .B1(multiplexer_6_out), .B2(multiplexer_7_out), .B3(multiplexer_8_out),
    .out_9(matrix_mult_1_out_9), .out_10(matrix_mult_1_out_10), .out_11(matrix_mult_1_out_11),
    .out_12(matrix_mult_1_out_12));
  Register #(.width(32)) register_1 (.D(matrix_mult_1_out_9), .Q(out_2), .clk(in_1));  // open: en, clr
  Register #(.width(32)) register_2 (.D(matrix_mult_1_out_10), .Q(out_3), .clk(in_1));  // open: en, clr
  Register #(.width(32)) register_3 (.D(matrix_mult_1_out_11), .Q(out_4), .clk(in_1));  // open: en, clr
  Register #(.width(32)) register_4 (.D(matrix_mult_1_out_12), .Q(out_5), .clk(in_1));  // open: en, clr
endmodule

module judge (
  input  in_1,
  input  [31:0] in_2,
  input  [31:0] in_3,
  input  [31:0] in_4,
  input  [31:0] in_5,
  output [31:0] out_6,
  output [31:0] out_7,
  output [31:0] out_8,
  output [31:0] out_9
);

  wire not_1_out;
  wire [31:0] unit_matr_1_out_1, unit_matr_1_out_2, unit_matr_1_out_3, unit_matr_1_out_4;

  not not_1 (not_1_out, in_1);
  unit_matr unit_matr_1 (
    .out_1(unit_matr_1_out_1), .out_2(unit_matr_1_out_2), .out_3(unit_matr_1_out_3), .out_4(unit_matr_1_out_4));
  Multiplexer #(.width(32)) multiplexer_1 (
    .in0(in_2), .in1(unit_matr_1_out_1), .out(out_6), .sel(not_1_out));  // open: en
  Multiplexer #(.width(32)) multiplexer_2 (
    .in0(in_3), .in1(unit_matr_1_out_2), .out(out_7), .sel(not_1_out));  // open: en
  Multiplexer #(.width(32)) multiplexer_3 (
    .in0(in_4), .in1(unit_matr_1_out_3), .out(out_8), .sel(not_1_out));  // open: en
  Multiplexer #(.width(32)) multiplexer_4 (
    .in0(in_5), .in1(unit_matr_1_out_4), .out(out_9), .sel(not_1_out));  // open: en
endmodule
