// Logisim project fsm-tem.circ as structural Verilog
module fsm (
  input  CLK,
  input  [1:0] In,
  output Z
);

  wire clock_1_out;
  wire [2:0] cao, qi, register_1_q;

  Multiplexer #(.width(3)) multiplexer_1 (.in0(cao), .in1(3'b000), .out(qi), .sel(CLK));  // open: en
  next_status next_status_1 (
    .S2(register_1_q[0]), .S1(register_1_q[1]), .S0(register_1_q[2]), .I1(In[1]), .I0(In[0]), .O2(cao[0]),
    .O1(cao[1]), .O0(cao[2]));
  Clock clock_1 (.out(clock_1_out));
  Register #(.width(3)) register_1 (.D(qi), .Q(register_1_q), .clk(clock_1_out));  // open: en, clr
  \output  output_1 (.S2(register_1_q[0]), .S1(register_1_q[1]), .S0(register_1_q[2]), .I1(In[1]), .I0(In[0]), .Z(Z));
endmodule

module next_status (
  input  S2,
  input  S1,
  input  S0,
  input  I1,
  input  I0,
  output O2,
  output O1,
  output O0
);

  wire and_2_out, and_3_out, and_4_out, and_5_out, and_6_out, and_7_out, and_8_out, and_9_out, not_1_out,
       not_2_out, not_3_out, not_4_out, not_5_out, not_6_out, not_7_out, not_8_out, not_9_out, not_10_out,
       not_11_out, not_12_out, not_13_out, not_14_out, not_15_out, not_16_out, not_17_out;

  not not_1 (not_1_out, I0);
  not not_2 (not_2_out, S1);
  not not_3 (not_3_out, I1);
  not not_4 (not_4_out, S1);
  not not_5 (not_5_out, I0);
  not not_6 (not_6_out, S0);
  not not_7 (not_7_out, I1);
  not not_8 (not_8_out, S0);
  not not_9 (not_9_out, I0);
  not not_10 (not_10_out, S1);
  not not_11 (not_11_out, S0);
  not not_12 (not_12_out, I1);
  not not_13 (not_13_out, S1);
  not not_14 (not_14_out, I0);
  not not_15 (not_15_out, S0);
  not not_16 (not_16_out, I0);
  not not_17 (not_17_out, I1);
  and and_1 (O2, S1, S0, not_1_out);
  and and_2 (and_2_out, not_2_out, S0, not_3_out);
  and and_3 (and_3_out, not_4_out, S0, not_5_out);
  and and_4 (and_4_out, S1, not_6_out, not_7_out);
  and and_5 (and_5_out, S1, not_8_out, not_9_out);
  and and_6 (and_6_out, not_10_out, not_11_out, not_12_out, I0);
  and and_7 (and_7_out, not_13_out, S0, not_14_out);
  and and_8 (and_8_out, S1, not_15_out, not_16_out);
  and and_9 (and_9_out, S1, S0, not_17_out, I0);
  or or_1 (O1, and_2_out, and_3_out, and_4_out, and_5_out);
  or or_2 (O0, and_6_out, and_7_out, and_8_out, and_9_out);
endmodule

module \output  (
  input  S2,
  input  S1,
  input  S0,
  input  I1,
  input  I0,
  output Z
);

  wire and_1_out, and_2_out, not_1_out, not_2_out, not_3_out, not_4_out, not_5_out;

  not not_1 (not_1_out, S2);
  not not_2 (not_2_out, I0);
  not not_3 (not_3_out, S2);
  not not_4 (not_4_out, I1);
  not not_5 (not_5_out, I0);
  and and_1 (and_1_out, not_1_out, S1, S0, I1, not_2_out);
  and and_2 (and_2_out, not_3_out, S1, S0, not_4_out, not_5_out);
  or or_1 (Z, and_1_out, and_2_out);
endmodule
