// Logisim project mod5.circ as structural Verilog
module mod5 (
  input  in_1,
  output s0,
  output s1,
  output s2,
  output s3,
  output s4
);

  wire clock_1_out, nand_1_out, not_1_out, not_2_out, not_3_out, not_4_out, not_5_out, register_2_q,
       register_3_q, register_4_q, register_5_q, xor_1_out;

  nand nand_1 (nand_1_out, register_5_q, register_2_q);
  xor xor_1 (xor_1_out, register_3_q, register_4_q);
  not not_1 (not_1_out, in_1);
  not not_2 (not_2_out, register_4_q);
  not not_3 (not_3_out, register_3_q);
  not not_4 (not_4_out, register_5_q);
  not not_5 (not_5_out, register_2_q);
  and and_1 (s1, not_2_out, not_1_out, nand_1_out, not_3_out);
  and and_2 (s2, not_2_out, in_1, nand_1_out, not_3_out);
  and and_3 (s3, not_4_out, in_1, xor_1_out, not_5_out);
  and and_4 (s4, not_4_out, not_1_out, xor_1_out, not_5_out);
  Clock clock_1 (.out(clock_1_out));
  Register #(.width(1)) register_1 (.D(s0), .Q(s0), .clk(clock_1_out));  // open: en, clr
  Register #(.width(1)) register_2 (.D(s1), .Q(register_2_q), .clk(clock_1_out));  // open: en, clr
  Register #(.width(1)) register_3 (.D(s2), .Q(register_3_q), .clk(clock_1_out));  // open: en, clr
  Register #(.width(1)) register_4 (.D(s3), .Q(register_4_q), .clk(clock_1_out));  // open: en, clr
  Register #(.width(1)) register_5 (.D(s4), .Q(register_5_q), .clk(clock_1_out));  // open: en, clr
endmodule
