// Logisim project sort.circ as structural Verilog
module _1bit_swap (
  input  I1,
  input  I2,
  input  S,
  output O1,
  output O2
);

  wire and_1_out, and_2_out, and_3_out, and_4_out, not_1_out, not_2_out;

  not not_1 (not_1_out, S);
  not not_2 (not_2_out, S);
  and and_1 (and_1_out, I1, not_1_out);
  and and_2 (and_2_out, I2, S);
  and and_3 (and_3_out, I2, not_2_out);
  and and_4 (and_4_out, I1, S);
  or or_1 (O1, and_1_out, and_2_out);
  or or_2 (O2, and_3_out, and_4_out);
endmodule

module _4bit_swap (
  input  [3:0] I1,
  input  [3:0] I2,
  output [3:0] O1,
  output [3:0] O2
);

  wire and_1_out, comparator_1_eq, comparator_1_gt, comparator_1_lt;
  wire [3:0] and_2_out, and_3_out, and_4_out, and_5_out, not_1_out, not_2_out;
  wire [3:3] or_1_out;

  Comparator #(.width(4), .mode("unsigned")) comparator_1 (
    .a(I1), .b(I2), .gt(comparator_1_gt), .eq(comparator_1_eq), .lt(comparator_1_lt));
  and and_1 (and_1_out, comparator_1_eq, comparator_1_lt);
  or or_1 (or_1_out[3], comparator_1_gt, and_1_out);
  // Probe on {4{or_1_out[3]}}
  assign not_1_out = ~{4{or_1_out[3]}};  // NOT_Gate not_1, 4 bits wide
  assign not_2_out = ~{4{or_1_out[3]}};  // NOT_Gate not_2, 4 bits wide
  assign and_2_out = I1 & not_1_out;  // AND_Gate and_2, 4 bits wide
  assign and_3_out = I2 & {4{or_1_out[3]}};  // AND_Gate and_3, 4 bits wide
  assign and_4_out = I2 & not_2_out;  // AND_Gate and_4, 4 bits wide
  assign and_5_out = I1 & {4{or_1_out[3]}};  // AND_Gate and_5, 4 bits wide
  assign O1 = and_2_out | and_3_out;  // OR_Gate or_2, 4 bits wide
  assign O2 = and_4_out | and_5_out;  // OR_Gate or_3, 4 bits wide
endmodule

module _4bit_sort (
  input  [3:0] in_1,
  input  [3:0] in_2,
  input  [3:0] in_3,
  input  [3:0] in_4,
  output [3:0] out_5,
  output [3:0] out_6,
  output [3:0] out_7,
  output [3:0] out_8
);

  wire [3:0] n4bit_swap_1_o1, n4bit_swap_1_o2, n4bit_swap_2_o1, n4bit_swap_2_o2, n4bit_swap_3_o1,
       n4bit_swap_3_o2, n4bit_swap_4_o1, n4bit_swap_4_o2;

  _4bit_swap u_4bit_swap_1 (.I1(in_1), .I2(in_2), .O1(n4bit_swap_1_o1), .O2(n4bit_swap_1_o2));
  // Probe on n4bit_swap_1_o2
  _4bit_swap u_4bit_swap_2 (.I1(in_3), .I2(in_4), .O1(n4bit_swap_2_o1), .O2(n4bit_swap_2_o2));
  _4bit_swap u_4bit_swap_3 (.I1(n4bit_swap_1_o2), .I2(n4bit_swap_2_o1), .O1(n4bit_swap_3_o1), .O2(n4bit_swap_3_o2));
  _4bit_swap u_4bit_swap_4 (.I1(n4bit_swap_1_o1), .I2(n4bit_swap_2_o2), .O1(n4bit_swap_4_o1), .O2(n4bit_swap_4_o2));
  _4bit_swap u_4bit_swap_5 (.I1(n4bit_swap_3_o1), .I2(n4bit_swap_4_o1), .O1(out_5), .O2(out_6));
  _4bit_swap u_4bit_swap_6 (.I1(n4bit_swap_3_o2), .I2(n4bit_swap_4_o2), .O1(out_7), .O2(out_8));
endmodule
