// Logisim project CPU.circ as structural Verilog: 7 circuits, main circuit main
// Op
module main (
  input  in_1,
  output [31:0] Instr,
  output RegWrite,
  output [4:0] RegAddr,
  output [31:0] RegData,
  output MemWrite,
  output [4:0] MemAddr,
  output [31:0] RegData_2
);

  wire ALUOp, ALUSrc, and_1_out, Branch, clk, Equal, Jump, MemRead, MemtoReg, MRtoShift, RegDst, ShiftMux;
  wire [2:0] alucontrol_1_out_4;
  wire [4:0] multiplexer_2_out, Rd, Rs, Rt, Shamt;
  wire [5:0] Func, Op;
  wire [15:0] Imme;
  wire [25:0] Addr;
  wire [31:0] adder_2_out, Address, bit_extender_1_out, bit_extender_2_out, Imm32, MemRdata,
       multiplexer_3_out, multiplexer_4_out, multiplexer_7_out, multiplexer_8_out, multiplexer_9_out, PC_4,
       Rdata1, Result, Shift, shifter_1_out, shifter_4_out;
  wire [31:5] MemAddr_t;

  Register #(.width(32)) PC (.D(multiplexer_9_out), .Q(Address), .clk(clk), .clr(in_1));  // open: en
  ControlUnit controlunit_1 (
    .Op(Op), .Func(Func), .Branch(Branch), .MemtoReg(MemtoReg), .MRtoShift(MRtoShift), .MemWrite(MemWrite),
    .MemRead(MemRead), .ALUOp(ALUOp), .ALUSrc(ALUSrc), .RegWrite(RegWrite), .RegDst(RegDst),
    .ShiftMux(ShiftMux), .Jump(Jump));
  Clock clock_1 (.out(clk));
  ROM #(.addrWidth(5), .dataWidth(32)) rom_1 ();  // open: addr, data, sel
  ROM #(.addrWidth(5), .dataWidth(32)) rom_2 (.addr(Address[4:0]), .data(Instr));  // open: sel
  Code_spli code_spli_1 (
    .in_1(Instr), .Func(Func), .Shamt(Shamt), .Rd(Rd), .Rt(Rt), .Rs(Rs), .Op(Op), .Imme(Imme), .Addr(Addr));
  // Probe on Instr
  // Probe on RegAddr
  // Probe on RegData
  // Probe on MemAddr
  // Probe on RegData_2
  assign bit_extender_1_out = {{16{Imme[15]}}, Imme};  // Bit_Extender bit_extender_1
  Multiplexer #(.width(32)) multiplexer_1 (
    .in0(bit_extender_1_out), .in1(bit_extender_2_out), .out(Imm32), .sel(ShiftMux));  // open: en
  assign bit_extender_2_out = {{16{1'b0}}, Imme};  // Bit_Extender bit_extender_2
  Shifter #(.width(32)) shifter_1 (.in(PC_4), .\dist (5'b00010), .out(shifter_1_out));
  Multiplexer #(.width(5)) multiplexer_2 (
    .in0({5{1'b0}}), .in1(5'b10000), .out(multiplexer_2_out), .sel(ShiftMux));  // open: en
  Multiplexer #(.width(32)) multiplexer_3 (
    .in0(Result), .in1(MemRdata), .out(multiplexer_3_out), .sel(MemtoReg));  // open: en
  Shifter #(.width(32)) shifter_2 (.in(Imm32), .\dist (multiplexer_2_out), .out(Shift));
  Adder #(.width(32)) adder_1 (.a(Address), .b(32'h1), .out(PC_4));  // open: cin, cout
  Multiplexer #(.width(32)) multiplexer_4 (
    .in0(multiplexer_3_out), .in1(Shift), .out(multiplexer_4_out), .sel(MRtoShift));  // open: en
  Multiplexer #(.width(32)) multiplexer_5 (
    .in0(multiplexer_4_out), .in1(shifter_1_out), .out(RegData), .sel(Jump));  // open: en
  Multiplexer #(.width(5)) multiplexer_6 (.in0(Rt), .in1(Rd), .out(RegAddr), .sel(RegDst));  // open: en
  GRF grf_1 (
    .A1(Rs), .A2(Rt), .A3(RegAddr), .WD(RegData), .clk(clk), .reset(in_1), .WE(RegWrite), .Output1(Rdata1),
    .Output2(RegData_2));
  Adder #(.width(32)) adder_2 (.a(PC_4), .b(Shift), .out(adder_2_out));  // open: cin, cout
  Shifter #(.width(32), .shift("lr")) shifter_3 (.in(Result), .\dist (5'b00010), .out({MemAddr_t, MemAddr}));
  Multiplexer #(.width(32)) multiplexer_7 (
    .in0(PC_4), .in1(adder_2_out), .out(multiplexer_7_out), .sel(and_1_out));  // open: en
  and and_1 (and_1_out, Branch, Equal);
  Shifter #(.width(32), .shift("ar")) shifter_4 (.in(Rdata1), .\dist (5'b00010), .out(shifter_4_out));
  Multiplexer #(.width(32)) multiplexer_8 (
    .in0(RegData_2), .in1(Imm32), .out(multiplexer_8_out), .sel(ALUSrc));  // open: en
  ALUControl alucontrol_1 (.Op(Op), .ALUOp(ALUOp), .Func(Func), .out_4(alucontrol_1_out_4));
  RAM #(.addrWidth(5), .dataWidth(32), .bus("separate")) ram_1 (
    .addr(MemAddr), .din(RegData_2), .data(MemRdata), .str(MemWrite), .clk(clk), .ld(MemRead), .clr(in_1));  // open: sel
  Multiplexer #(.width(32)) multiplexer_9 (
    .in0(multiplexer_7_out), .in1(shifter_4_out), .out(multiplexer_9_out), .sel(Jump));  // open: en
  ALU alu_1 (.data1(Rdata1), .data2(multiplexer_8_out), .equal(Equal), .result(Result), .op(alucontrol_1_out_4));

  // Other names for the same wires on the sheet: MemAddr_t[4:0] = MemAddr; Rdata2[31:0] = RegData_2; Reset = in_1
endmodule

module ControlUnit (
  input  [5:0] Op,
  input  [5:0] Func,
  output Branch,
  output MemtoReg,
  output MRtoShift,
  output MemWrite,
  output MemRead,
  output ALUOp,
  output ALUSrc,
  output RegWrite,
  output RegDst,
  output ShiftMux,
  output Jump
);

  wire addiu_out, Jalr_out, or_2_out, ori_out;

  and R_format (ALUOp, ~Op[5], ~Op[4], ~Op[3], ~Op[2], ~Op[1], ~Op[0]);  // AND_Gate
  and Jalr (Jalr_out, ~Func[5], ~Func[4], Func[3], ~Func[2], ~Func[1], Func[0]);  // AND_Gate
  and ori (ori_out, ~Op[5], ~Op[4], Op[3], Op[2], ~Op[1], Op[0]);  // AND_Gate
  and lw (MemRead, Op[5], ~Op[4], ~Op[3], ~Op[2], Op[1], Op[0]);  // AND_Gate
  and sw (MemWrite, Op[5], ~Op[4], Op[3], ~Op[2], Op[1], Op[0]);  // AND_Gate
  and beq (Branch, ~Op[5], ~Op[4], ~Op[3], Op[2], ~Op[1], ~Op[0]);  // AND_Gate
  and lui (MRtoShift, ~Op[5], ~Op[4], Op[3], Op[2], Op[1], Op[0]);  // AND_Gate
  and addiu (addiu_out, ~Op[5], ~Op[4], Op[3], ~Op[2], ~Op[1], Op[0]);  // AND_Gate
  or or_1 (ALUSrc, MemRead, ori_out, MemWrite, addiu_out);
  or or_2 (or_2_out, addiu_out, ALUOp, MRtoShift, MemRead, ori_out);
  or or_3 (ShiftMux, ori_out, MRtoShift);
  and and_1 (Jump, Jalr_out, ALUOp);
  or or_4 (RegWrite, or_2_out, Jump);
  or notice_000000 (RegDst, ALUOp, Jump);

  assign MemtoReg = MemRead;

  // Other names for the same wires on the sheet: R_Format = ALUOp
endmodule

// Func
module ALUControl (
  input  [5:0] Op,
  input  ALUOp,
  input  [5:0] Func,
  output [2:0] out_4
);

  wire and_1_out, and_2_out, and_3_out, and_4_out, and_5_out, and_6_out, and_7_out, and_8_out, and_9_out;

  and and_1 (and_1_out, ~Op[5], ~Op[4], Op[3], Op[2], ~Op[1], Op[0]);  // AND_Gate
  and and_2 (and_2_out, Func[5], ~Func[4], ~Func[3], ~Func[2], ~Func[1], Func[0]);  // AND_Gate
  and and_3 (and_3_out, Op[5], ~Op[4], Op[3], ~Op[2], Op[1], Op[0]);  // AND_Gate
  and and_4 (and_4_out, Func[5], ~Func[4], ~Func[3], ~Func[2], Func[1], Func[0]);  // AND_Gate
  and and_5 (and_5_out, Op[5], ~Op[4], ~Op[3], ~Op[2], Op[1], Op[0]);  // AND_Gate
  and and_6 (and_6_out, ~Op[5], ~Op[4], Op[3], ~Op[2], ~Op[1], Op[0]);  // AND_Gate
  and and_7 (and_7_out, ALUOp, and_2_out);
  and and_8 (and_8_out, ALUOp, and_4_out);
  and and_9 (and_9_out, ALUOp, 1'b0, 1'b0);
  or or_1 (out_4[0], and_5_out, and_6_out, and_7_out, and_3_out);
  buf or_2 (out_4[1], and_8_out);  // OR_Gate
  or or_3 (out_4[2], and_9_out, and_1_out);
endmodule

module Code_spli (
  input  [31:0] in_1,
  output [5:0] Func,
  output [4:0] Shamt,
  output [4:0] Rd,
  output [4:0] Rt,
  output [4:0] Rs,
  output [5:0] Op,
  output [15:0] Imme,
  output [25:0] Addr
);


  assign Addr = in_1[25:0];
  assign Func = in_1[5:0];
  assign Imme = in_1[15:0];
  assign Op = in_1[31:26];
  assign Rd = in_1[15:11];
  assign Rs = in_1[25:21];
  assign Rt = in_1[20:16];
  assign Shamt = in_1[10:6];
endmodule

module ALU (
  input  [31:0] data1,
  input  [31:0] data2,
  input  [2:0] op,
  output equal,
  output [31:0] result
);

  wire [31:0] adder_1_out, and_1_out, or_1_out, subtractor_1_out;

  Adder #(.width(32)) adder_1 (.a(data1), .b(data2), .out(adder_1_out));  // open: cin, cout
  Subtractor #(.width(32)) subtractor_1 (.a(data1), .b(data2), .out(subtractor_1_out));  // open: bin, bout
  assign and_1_out = data1 & data2;  // AND_Gate and_1, 32 bits wide
  assign or_1_out = data1 | data2;  // OR_Gate or_1, 32 bits wide
  Comparator #(.width(32)) comparator_1 (.a(data1), .b(data2), .eq(equal));  // open: gt, lt
  Multiplexer #(.select(3), .width(32)) multiplexer_1 (
    .in0({32{1'b0}}), .in1(adder_1_out), .in2(subtractor_1_out), .in3(and_1_out), .in4(or_1_out),
    .out(result), .sel(op));  // open: in5, in6, in7, en
endmodule

module GRF (
  input  clk,
  input  reset,
  input  WE,
  input  [4:0] A1,
  input  [4:0] A2,
  input  [4:0] A3,
  input  [31:0] WD,
  output [31:0] Output1,
  output [31:0] Output2
);

  RegGroup reggroup_1 (
    .clk(clk), .A1(A1), .A2(A2), .A3(A3), .en(WE), .in_6(WD), .reset(reset), .A1_2(Output1), .A2_2(Output2));
endmodule

module RegGroup (
  input  clk,
  input  [4:0] A1,
  input  [4:0] A2,
  input  [4:0] A3,
  input  en,
  input  [31:0] in_6,
  input  reset,
  output [31:0] A1_2,
  output [31:0] A2_2
);

  wire E0, E1, E2, E3, E4, E5, E6, E7, E8, E9, E10, E11, E12, E13, E14, E15, E16, E17, E18, E19, E20, E21,
       E22, E23, E24, E25, E26, E27, E28, E29, E30, E31;
  wire [31:0] D1, D2, D3, D4, D5, D6, D7, D8, D9, D10, D11, D12, D13, D14, D15, D16, D17, D18, D19, D20, D21,
       D22, D23, D24, D25, D26, D27, D28, D29, D30, D31, Q0, Q1, Q2, Q3, Q4, Q5, Q6, Q7, Q8, Q9, Q10, Q11,
       Q12, Q13, Q14, Q15, Q16, Q17, Q18, Q19, Q20, Q21, Q22, Q23, Q24, Q25, Q26, Q27, Q28, Q29, Q30, Q31;

  Demultiplexer #(.select(5), .width(32), .enable("false")) demultiplexer_1 (
    .out1(D1), .out2(D2), .out3(D3), .out4(D4), .out5(D5), .out6(D6), .out7(D7), .out8(D8), .out9(D9),
    .out10(D10), .out11(D11), .out12(D12), .out13(D13), .out14(D14), .out15(D15), .out16(D16), .out17(D17),
    .out18(D18), .out19(D19), .out20(D20), .out21(D21), .out22(D22), .out23(D23), .out24(D24), .out25(D25),
    .out26(D26), .out27(D27), .out28(D28), .out29(D29), .out30(D30), .out31(D31), .in(in_6), .sel(A3));  // open: out0
  Register #(.width(32)) _0 (.D({32{1'b0}}), .en(E0), .Q(Q0), .clk(clk), .clr(reset));
  Register #(.width(32)) _8 (.D(D8), .en(E8), .Q(Q8), .clk(clk), .clr(reset));
  Register #(.width(32)) _16 (.D(D16), .en(E16), .Q(Q16), .clk(clk), .clr(reset));
  Register #(.width(32)) _24 (.D(D24), .en(E24), .Q(Q24), .clk(clk), .clr(reset));
  Register #(.width(32)) _1 (.D(D1), .en(E1), .Q(Q1), .clk(clk), .clr(reset));
  Register #(.width(32)) _9 (.D(D9), .en(E9), .Q(Q9), .clk(clk), .clr(reset));
  Register #(.width(32)) _17 (.D(D17), .en(E17), .Q(Q17), .clk(clk), .clr(reset));
  Register #(.width(32)) _25 (.D(D25), .en(E25), .Q(Q25), .clk(clk), .clr(reset));
  Register #(.width(32)) _2 (.D(D2), .en(E2), .Q(Q2), .clk(clk), .clr(reset));
  Register #(.width(32)) _10 (.D(D10), .en(E10), .Q(Q10), .clk(clk), .clr(reset));
  Register #(.width(32)) _18 (.D(D18), .en(E18), .Q(Q18), .clk(clk), .clr(reset));
  Register #(.width(32)) _26 (.D(D26), .en(E26), .Q(Q26), .clk(clk), .clr(reset));
  Register #(.width(32)) _3 (.D(D3), .en(E3), .Q(Q3), .clk(clk), .clr(reset));
  Register #(.width(32)) _11 (.D(D11), .en(E11), .Q(Q11), .clk(clk), .clr(reset));
  Register #(.width(32)) _19 (.D(D19), .en(E19), .Q(Q19), .clk(clk), .clr(reset));
  Register #(.width(32)) _27 (.D(D27), .en(E27), .Q(Q27), .clk(clk), .clr(reset));
  Demultiplexer #(.select(5), .enable("false")) demultiplexer_2 (
    .out0(E0), .out1(E1), .out2(E2), .out3(E3), .out4(E4), .out5(E5), .out6(E6), .out7(E7), .out8(E8),
    .out9(E9), .out10(E10), .out11(E11), .out12(E12), .out13(E13), .out14(E14), .out15(E15), .out16(E16),
    .out17(E17), .out18(E18), .out19(E19), .out20(E20), .out21(E21), .out22(E22), .out23(E23), .out24(E24),
    .out25(E25), .out26(E26), .out27(E27), .out28(E28), .out29(E29), .out30(E30), .out31(E31), .in(en),
    .sel(A3));
  Register #(.width(32)) _4 (.D(D4), .en(E4), .Q(Q4), .clk(clk), .clr(reset));
  Register #(.width(32)) _12 (.D(D12), .en(E12), .Q(Q12), .clk(clk), .clr(reset));
  Register #(.width(32)) _20 (.D(D20), .en(E20), .Q(Q20), .clk(clk), .clr(reset));
  Register #(.width(32)) _28 (.D(D28), .en(E28), .Q(Q28), .clk(clk), .clr(reset));
  Register #(.width(32)) _5 (.D(D5), .en(E5), .Q(Q5), .clk(clk), .clr(reset));
  Register #(.width(32)) _13 (.D(D13), .en(E13), .Q(Q13), .clk(clk), .clr(reset));
  Register #(.width(32)) _21 (.D(D21), .en(E21), .Q(Q21), .clk(clk), .clr(reset));
  Register #(.width(32)) _29 (.D(D29), .en(E29), .Q(Q29), .clk(clk), .clr(reset));
  Register #(.width(32)) _6 (.D(D6), .en(E6), .Q(Q6), .clk(clk), .clr(reset));
  Register #(.width(32)) _14 (.D(D14), .en(E14), .Q(Q14), .clk(clk), .clr(reset));
  Register #(.width(32)) _22 (.D(D22), .en(E22), .Q(Q22), .clk(clk), .clr(reset));
  Register #(.width(32)) _30 (.D(D30), .en(E30), .Q(Q30), .clk(clk), .clr(reset));
  Register #(.width(32)) _7 (.D(D7), .en(E7), .Q(Q7), .clk(clk), .clr(reset));
  Register #(.width(32)) _15 (.D(D15), .en(E15), .Q(Q15), .clk(clk), .clr(reset));
  Register #(.width(32)) _23 (.D(D23), .en(E23), .Q(Q23), .clk(clk), .clr(reset));
  Register #(.width(32)) _31 (.D(D31), .en(E31), .Q(Q31), .clk(clk), .clr(reset));
  Multiplexer #(.select(5), .width(32)) multiplexer_1 (
    .in0(Q0), .in1(Q1), .in2(Q2), .in3(Q3), .in4(Q4), .in5(Q5), .in6(Q6), .in7(Q7), .in8(Q8), .in9(Q9),
    .in10(Q10), .in11(Q11), .in12(Q12), .in13(Q13), .in14(Q14), .in15(Q15), .in16(Q16), .in17(Q17),
    .in18(Q18), .in19(Q19), .in20(Q20), .in21(Q21), .in22(Q22), .in23(Q23), .in24(Q24), .in25(Q25),
    .in26(Q26), .in27(Q27), .in28(Q28), .in29(Q29), .in30(Q30), .in31(Q31), .out(A1_2), .sel(A1));  // open: en
  Multiplexer #(.select(5), .width(32)) multiplexer_2 (
    .in0(Q0), .in1(Q1), .in2(Q2), .in3(Q3), .in4(Q4), .in5(Q5), .in6(Q6), .in7(Q7), .in8(Q8), .in9(Q9),
    .in10(Q10), .in11(Q11), .in12(Q12), .in13(Q13), .in14(Q14), .in15(Q15), .in16(Q16), .in17(Q17),
    .in18(Q18), .in19(Q19), .in20(Q20), .in21(Q21), .in22(Q22), .in23(Q23), .in24(Q24), .in25(Q25),
    .in26(Q26), .in27(Q27), .in28(Q28), .in29(Q29), .in30(Q30), .in31(Q31), .out(A2_2), .sel(A2));  // open: en

  // Other names for the same wires on the sheet: in[31:0] = in_6
endmodule
